// Logisim project CPU_single_circle.circ as structural Verilog
module main (
);

  wire alu_1_p4, and_1_out, clock_1_out, comparator_1_eq, main_control_1_lw, main_control_1_sw,
       main_control_1_syscall, main_control_1_we, main_control_1_x_op, multiplexer_1_out;
  wire [1:0] main_control_1_din_op, main_control_1_pc_op, main_control_1_rw_op, main_control_1_y_op;
  wire [3:0] main_1_p6_2, main_1_p6_3, main_1_p6_4, main_1_p6_5, main_control_1_alu_op;
  wire [4:0] main_control_1_rd, main_control_1_rs, main_control_1_rt, multiplexer_3_out;
  wire [15:0] main_1_p6;
  wire [31:0] adder_1_out, adder_2_out, alu_1_p5, and_2_out, counter_1_q, main_1_p5, main_1_p9, main_1_p10,
       main_control_1_imm_15, main_control_1_imm_26_2, main_control_1_shamt, multiplexer_2_out,
       multiplexer_5_out, multiplexer_6_out, or_1_out, ram_1_data, reg2, register_1_q, rom_1_data,
       shifter_1_out;

  Clock clock_1 (.out(clock_1_out));
  Multiplexer #(.enable("false")) multiplexer_1 (
    .in0(clock_1_out), .in1(1'b1), .out(multiplexer_1_out), .sel(and_1_out));
  Counter #(.width(32), .max('hffffffff)) counter_1 (
    .load(1'b0), .count(1'b1), .Q(counter_1_q), .clk(multiplexer_1_out));  // open: D, carry, clr
  Register #(.width(32), .trigger("falling")) register_1 (
    .D(multiplexer_2_out), .Q(register_1_q), .clk(multiplexer_1_out));  // open: en, clr
  // Probe on counter_1_q
  and and_1 (and_1_out, main_control_1_syscall, comparator_1_eq);
  Comparator #(.width(32)) comparator_1 (.a(32'ha), .b(reg2), .eq(comparator_1_eq));  // open: gt, lt
  Adder #(.width(32)) adder_1 (.a(32'h4), .b(register_1_q), .out(adder_1_out));  // open: cin, cout
  assign and_2_out = register_1_q & 32'hf0000000;  // AND_Gate and_2, 32 bits wide
  ROM #(.addrWidth(10), .dataWidth(32)) rom_1 (.addr(register_1_q[11:2]), .data(rom_1_data), .sel(1'b1));
  Multiplexer #(.select(2), .width(32), .enable("false")) multiplexer_2 (
    .in0(adder_1_out), .in1(main_1_p9), .in2(or_1_out), .in3(adder_2_out), .out(multiplexer_2_out),
    .sel(main_control_1_pc_op));
  main_control main_control_1 (
    .PC(rom_1_data), .rw_op(main_control_1_rw_op), .x_op(main_control_1_x_op), .y_op(main_control_1_y_op),
    .alu_op(main_control_1_alu_op), .syscall(main_control_1_syscall), .sw(main_control_1_sw),
    .lw(main_control_1_lw), .rs(main_control_1_rs), .rt(main_control_1_rt), .rd(main_control_1_rd),
    .imm_15(main_control_1_imm_15), .shamt(main_control_1_shamt), .imm_26_2(main_control_1_imm_26_2),
    .equal(alu_1_p4), .pc_op(main_control_1_pc_op), .din_op(main_control_1_din_op), .we(main_control_1_we));
  assign or_1_out = and_2_out | main_control_1_imm_26_2;  // OR_Gate or_1, 32 bits wide
  Adder #(.width(32)) adder_2 (.a(adder_1_out), .b(shifter_1_out), .out(adder_2_out));  // open: cin, cout
  Shifter #(.width(32)) shifter_1 (.in(main_control_1_imm_15), .\dist (5'b00010), .out(shifter_1_out));
  Multiplexer #(.select(2), .width(5), .enable("false")) multiplexer_3 (
    .in0(main_control_1_rd), .in1(main_control_1_rt), .in2({5{1'b1}}), .out(multiplexer_3_out),
    .sel(main_control_1_rw_op));  // open: in3
  // regfile_main main_1: pin names not known; wires that end beside it: main_control_1_rs, main_control_1_rt, multiplexer_3_out, reg2, main_1_p5, {main_1_p6_5, main_1_p6_4, main_1_p6_3, main_1_p6_2, main_1_p6}, main_control_1_we, multiplexer_1_out, main_1_p9, main_1_p10
  Multiplexer #(.select(2), .width(32), .enable("false")) multiplexer_4 (
    .in0(alu_1_p5), .in1(ram_1_data), .in2(adder_1_out), .out(main_1_p5), .sel(main_control_1_din_op));  // open: in3
  Multiplexer #(.width(32), .enable("false")) multiplexer_5 (
    .in0(main_1_p9), .in1(main_1_p10), .out(multiplexer_5_out), .sel(main_control_1_x_op));
  Multiplexer #(.select(2), .width(32), .enable("false")) multiplexer_6 (
    .in0(main_1_p10), .in1(main_control_1_shamt), .in2(main_control_1_imm_15), .out(multiplexer_6_out),
    .sel(main_control_1_y_op));  // open: in3
  // ALU alu_1: pin names not known; wires that end beside it: multiplexer_5_out, multiplexer_6_out, main_control_1_alu_op, alu_1_p4, alu_1_p5
  Hex_Digit_Display hex_digit_display_1 (.value(main_1_p6_5));  // open: dp
  Hex_Digit_Display hex_digit_display_2 (.value(main_1_p6_4));  // open: dp
  Hex_Digit_Display hex_digit_display_3 (.value(main_1_p6_3));  // open: dp
  Hex_Digit_Display hex_digit_display_4 (.value(main_1_p6_2));  // open: dp
  Hex_Digit_Display hex_digit_display_5 (.value(main_1_p6[15:12]));  // open: dp
  Hex_Digit_Display hex_digit_display_6 (.value(main_1_p6[11:8]));  // open: dp
  Hex_Digit_Display hex_digit_display_7 (.value(main_1_p6[7:4]));  // open: dp
  Hex_Digit_Display hex_digit_display_8 (.value(main_1_p6[3:0]));  // open: dp
  RAM #(.addrWidth(10), .dataWidth(32), .bus("separate")) ram_1 (
    .addr(alu_1_p5[11:2]), .din(main_1_p10), .data(ram_1_data), .str(main_control_1_sw), .sel(1'b1),
    .clk(multiplexer_1_out), .ld(main_control_1_lw));  // open: clr

  // Notes on the sheet:
  //   contents of rom_1 (hex, n*v repeats v):
  //   20110001 8000c05 20110001 20120002 20130003 8000c09 20110001 20120002 20130003 8000c0d 20110001
  //   20120002 20130003 8000c11 20110001 20120002 20130003 c000cb8 20100001 20110001 118fc0 112020
  //   20020022 c 118882 12200001 8000c15 112020 20020022 c 20110001 118880 112020 20020022 c 12200001
  //   8000c1f 20110001 118fc0 112020 20020022 c 1188c3 112020 20020022 c 118903 112020 20020022 c 118903
  //   112020 20020022 c 118903 112020 20020022 c 118903 112020 20020022 c 118903 112020 20020022 c 118903
  //   112020 20020022 c 118903 112020 20020022 c 20100001 109fc0 139fc3 8021 2012000c 24160003 26100001
  //   3210000f 20080008 20090001 139900 2709825 132020 20020022 c 1094022 1500fff9 22100001 2018000f
  //   2188024 108700 20080008 20090001 139902 2709825 132021 20020022 c 1094022 1500fff9 108702 2c9b022
  //   12c00001 8000c50 4020 1084027 84400 3508ffff 82021 20020022 c 2010ffff 20110000 ae300000 22100001
  //   22310004 ae300000 22100001 22310004 ae300000 22100001 22310004 ae300000 22100001 22310004 ae300000
  //   22100001 22310004 ae300000 22100001 22310004 ae300000 22100001 22310004 ae300000 22100001 22310004
  //   ae300000 22100001 22310004 ae300000 22100001 22310004 ae300000 22100001 22310004 ae300000 22100001
  //   22310004 ae300000 22100001 22310004 ae300000 22100001 22310004 ae300000 22100001 22310004 ae300000
  //   22100001 22310004 22100001 8020 2011003c 8e130000 8e340000 274402a 11000002 ae330000 ae140000
  //   2231fffc 1611fff8 102020 20020022 c 22100004 2011003c 1611fff2 2002000a c 20100000 22100001 102020
  //   20020022 c 22100002 102020 20020022 c 22100003 102020 20020022 c 22100004 102020 20020022 c 22100005
  //   102020 20020022 c 22100006 102020 20020022 c 22100007 102020 20020022 c 22100008 102020 20020022
  //   20020022 c 3e00008
endmodule

module \I型指令  (
  input  op0,
  input  op1,
  input  op2,
  input  op3,
  input  op4,
  input  op5,
  output addi,
  output addiu,
  output andi,
  output ori,
  output lw,
  output sw,
  output beq,
  output bne,
  output slti
);

  wire not_1_out, not_2_out, not_3_out, not_4_out, not_5_out, not_6_out, not_7_out, not_8_out, not_9_out,
       not_10_out, not_11_out, not_12_out, not_13_out, not_14_out, not_15_out, not_16_out, not_17_out,
       not_18_out, not_19_out, not_20_out, not_21_out, not_22_out, not_23_out, not_24_out, not_25_out,
       not_26_out, not_27_out, not_28_out, not_29_out, not_30_out, not_31_out, not_32_out, not_33_out,
       not_34_out;

  not not_1 (not_1_out, op0);
  not not_2 (not_2_out, op1);
  not not_3 (not_3_out, op3);
  not not_4 (not_4_out, op4);
  not not_5 (not_5_out, op5);
  not not_6 (not_6_out, op0);
  not not_7 (not_7_out, op1);
  not not_8 (not_8_out, op3);
  not not_9 (not_9_out, op4);
  not not_10 (not_10_out, op0);
  not not_11 (not_11_out, op1);
  not not_12 (not_12_out, op4);
  not not_13 (not_13_out, op5);
  not not_14 (not_14_out, op0);
  not not_15 (not_15_out, op1);
  not not_16 (not_16_out, op4);
  not not_17 (not_17_out, op1);
  not not_18 (not_18_out, op2);
  not not_19 (not_19_out, op3);
  not not_20 (not_20_out, op1);
  not not_21 (not_21_out, op3);
  not not_22 (not_22_out, op0);
  not not_23 (not_23_out, op1);
  not not_24 (not_24_out, op2);
  not not_25 (not_25_out, op4);
  not not_26 (not_26_out, op5);
  not not_27 (not_27_out, op0);
  not not_28 (not_28_out, op1);
  not not_29 (not_29_out, op2);
  not not_30 (not_30_out, op4);
  not not_31 (not_31_out, op0);
  not not_32 (not_32_out, op1);
  not not_33 (not_33_out, op3);
  not not_34 (not_34_out, op5);
  and and_1 (addi, not_1_out, not_2_out, op2, not_3_out, not_4_out, not_5_out);
  and and_2 (addiu, not_6_out, not_7_out, op2, not_8_out, not_9_out, op5);
  and and_3 (andi, not_10_out, not_11_out, op2, op3, not_12_out, not_13_out);
  and and_4 (ori, not_14_out, not_15_out, op2, op3, not_16_out, op5);
  and and_5 (lw, op0, not_17_out, not_18_out, not_19_out, op4, op5);
  and and_6 (sw, op0, not_20_out, op2, not_21_out, op4, op5);
  and and_7 (beq, not_22_out, not_23_out, not_24_out, op3, not_25_out, not_26_out);
  and and_8 (bne, not_27_out, not_28_out, not_29_out, op3, not_30_out, op5);
  and and_9 (slti, not_31_out, not_32_out, op2, not_33_out, op4, not_34_out);
endmodule

module \R型指令  (
  input  funct0,
  input  funct1,
  input  funct2,
  input  funct3,
  input  funct4,
  input  funct5,
  input  in_7,
  output add,
  output addu,
  output \and ,
  output sll,
  output sra,
  output srl,
  output sub,
  output \or ,
  output \nor ,
  output slt,
  output sltu,
  output syscall,
  output jr
);

  wire and_1_out, and_2_out, and_3_out, and_4_out, and_5_out, and_6_out, and_7_out, and_8_out, and_9_out,
       and_10_out, and_11_out, and_12_out, and_13_out, not_1_out, not_2_out, not_3_out, not_4_out, not_5_out,
       not_6_out, not_7_out, not_8_out, not_9_out, not_10_out, not_11_out, not_12_out, not_13_out,
       not_14_out, not_15_out, not_16_out, not_17_out, not_18_out, not_19_out, not_20_out, not_21_out,
       not_22_out, not_23_out, not_24_out, not_25_out, not_26_out, not_27_out, not_28_out, not_29_out,
       not_30_out, not_31_out, not_32_out, not_33_out, not_34_out, not_35_out, not_36_out, not_37_out,
       not_38_out, not_39_out, not_40_out, not_41_out, not_42_out, not_43_out, not_44_out, not_45_out,
       not_46_out, not_47_out, not_48_out, not_49_out, not_50_out, not_51_out;

  not not_1 (not_1_out, funct1);
  not not_2 (not_2_out, funct2);
  not not_3 (not_3_out, funct3);
  not not_4 (not_4_out, funct4);
  not not_5 (not_5_out, funct5);
  not not_6 (not_6_out, funct1);
  not not_7 (not_7_out, funct2);
  not not_8 (not_8_out, funct3);
  not not_9 (not_9_out, funct4);
  not not_10 (not_10_out, funct1);
  not not_11 (not_11_out, funct2);
  not not_12 (not_12_out, funct4);
  not not_13 (not_13_out, funct5);
  not not_14 (not_14_out, funct0);
  not not_15 (not_15_out, funct1);
  not not_16 (not_16_out, funct2);
  not not_17 (not_17_out, funct3);
  not not_18 (not_18_out, funct4);
  not not_19 (not_19_out, funct5);
  not not_20 (not_20_out, funct0);
  not not_21 (not_21_out, funct1);
  not not_22 (not_22_out, funct2);
  not not_23 (not_23_out, funct3);
  not not_24 (not_24_out, funct0);
  not not_25 (not_25_out, funct1);
  not not_26 (not_26_out, funct2);
  not not_27 (not_27_out, funct3);
  not not_28 (not_28_out, funct5);
  not not_29 (not_29_out, funct1);
  not not_30 (not_30_out, funct2);
  not not_31 (not_31_out, funct3);
  not not_32 (not_32_out, funct5);
  not not_33 (not_33_out, funct1);
  not not_34 (not_34_out, funct2);
  not not_35 (not_35_out, funct4);
  not not_36 (not_36_out, funct1);
  not not_37 (not_37_out, funct2);
  not not_38 (not_38_out, funct1);
  not not_39 (not_39_out, funct3);
  not not_40 (not_40_out, funct5);
  not not_41 (not_41_out, funct1);
  not not_42 (not_42_out, funct3);
  not not_43 (not_43_out, funct0);
  not not_44 (not_44_out, funct1);
  not not_45 (not_45_out, funct4);
  not not_46 (not_46_out, funct5);
  not not_47 (not_47_out, funct0);
  not not_48 (not_48_out, funct1);
  not not_49 (not_49_out, funct3);
  not not_50 (not_50_out, funct4);
  not not_51 (not_51_out, funct5);
  and and_1 (and_1_out, funct0, not_1_out, not_2_out, not_3_out, not_4_out, not_5_out);
  and and_2 (and_2_out, funct0, not_6_out, not_7_out, not_8_out, not_9_out, funct5);
  and and_3 (and_3_out, funct0, not_10_out, not_11_out, funct3, not_12_out, not_13_out);
  and and_4 (and_4_out, not_14_out, not_15_out, not_16_out, not_17_out, not_18_out, not_19_out);
  and and_5 (and_5_out, not_20_out, not_21_out, not_22_out, not_23_out, funct4, funct5);
  and and_6 (and_6_out, not_24_out, not_25_out, not_26_out, not_27_out, funct4, not_28_out);
  and and_7 (and_7_out, funct0, not_29_out, not_30_out, not_31_out, funct4, not_32_out);
  and and_8 (and_8_out, funct0, not_33_out, not_34_out, funct3, not_35_out, funct5);
  and and_9 (and_9_out, funct0, not_36_out, not_37_out, funct3, funct4, funct5);
  and and_10 (and_10_out, funct0, not_38_out, funct2, not_39_out, funct4, not_40_out);
  and and_11 (and_11_out, funct0, not_41_out, funct2, not_42_out, funct4, funct5);
  and and_12 (and_12_out, not_43_out, not_44_out, funct2, funct3, not_45_out, not_46_out);
  and and_13 (and_13_out, not_47_out, not_48_out, funct2, not_49_out, not_50_out, not_51_out);
  and and_14 (add, and_1_out, in_7);
  and and_15 (addu, and_2_out, in_7);
  and and_16 (\and , and_3_out, in_7);
  and and_17 (sll, and_4_out, in_7);
  and and_18 (sra, and_5_out, in_7);
  and and_19 (srl, and_6_out, in_7);
  and and_20 (sub, and_7_out, in_7);
  and and_21 (\or , and_8_out, in_7);
  and and_22 (\nor , and_9_out, in_7);
  and and_23 (slt, and_10_out, in_7);
  and and_24 (sltu, and_11_out, in_7);
  and and_25 (syscall, and_12_out, in_7);
  and and_26 (jr, and_13_out, in_7);
endmodule

module \j型指令  (
  input  op0,
  input  op1,
  input  op2,
  input  op3,
  input  op4,
  input  op5,
  output j,
  output jal
);

  wire not_1_out, not_2_out, not_3_out, not_4_out, not_5_out, not_6_out, not_7_out, not_8_out, not_9_out;

  not not_1 (not_1_out, op0);
  not not_2 (not_2_out, op1);
  not not_3 (not_3_out, op2);
  not not_4 (not_4_out, op3);
  not not_5 (not_5_out, op5);
  not not_6 (not_6_out, op0);
  not not_7 (not_7_out, op1);
  not not_8 (not_8_out, op2);
  not not_9 (not_9_out, op3);
  and and_1 (j, not_1_out, not_2_out, not_3_out, not_4_out, op4, not_5_out);
  and and_2 (jal, not_6_out, not_7_out, not_8_out, not_9_out, op4, op5);
endmodule

module signal (
  input  [31:0] PC,
  output add,
  output addu,
  output \and ,
  output sll,
  output sra,
  output srl,
  output sub,
  output \or ,
  output \nor ,
  output slt,
  output sltu,
  output syscall,
  output jr,
  output j,
  output jal,
  output addi,
  output addiu,
  output andi,
  output ori,
  output lw,
  output sw,
  output beq,
  output bne,
  output slti
);

  wire and_1_out;

  and and_1 (and_1_out, ~PC[31], ~PC[30], ~PC[29], ~PC[28], ~PC[27], ~PC[26]);  // AND_Gate
  \R型指令  \r型指令_1  (
    .funct0(PC[5]), .funct1(PC[4]), .funct2(PC[3]), .funct3(PC[2]), .funct4(PC[1]), .funct5(PC[0]),
    .in_7(and_1_out), .add(add), .addu(addu), .\and (\and ), .sll(sll), .sra(sra), .srl(srl), .sub(sub),
    .\or (\or ), .\nor (\nor ), .slt(slt), .sltu(sltu), .syscall(syscall), .jr(jr));
  \j型指令  \j型指令_1  (
    .op0(PC[31]), .op1(PC[30]), .op2(PC[29]), .op3(PC[28]), .op4(PC[27]), .op5(PC[26]), .j(j), .jal(jal));
  \I型指令  \i型指令_1  (
    .op0(PC[31]), .op1(PC[30]), .op2(PC[29]), .op3(PC[28]), .op4(PC[27]), .op5(PC[26]), .addi(addi),
    .addiu(addiu), .andi(andi), .ori(ori), .lw(lw), .sw(sw), .beq(beq), .bne(bne), .slti(slti));
endmodule

module OP_control (
  input  SLL,
  input  ADD,
  input  ADDU,
  input  ADDI,
  input  ADDIU,
  input  AND,
  input  ANDI,
  input  LW,
  input  SW,
  input  SRL,
  input  SRA,
  input  OR,
  input  ORI,
  input  NOR,
  input  SLT,
  input  SLTI,
  input  SLTU,
  input  SUB,
  output [3:0] out_19
);

  and and_1 (out_19[0], ~SUB, ~SLL, ~SRL, ~OR, ~ORI);  // AND_Gate
  and and_2 (out_19[1], ~SLL, ~SRA, ~ADD, ~ADDI, ~ADDU, ~ORI, ~ADDIU, ~SW, ~LW, ~OR, ~NOR);  // AND_Gate
  and and_3 (out_19[2], ~SLL, ~NOR, ~SRA, ~SLTU, ~SRL, ~SLTI, ~ORI, ~SLT, ~OR);  // AND_Gate
  and and_4 (out_19[3], ~SLL, ~SRA, ~SRL, ~ADD, ~ADDI, ~ADDU, ~ADDIU, ~SW, ~LW, ~SUB, ~AND, ~ANDI);  // AND_Gate
endmodule

module main_control (
  input  equal,
  input  [31:0] PC,
  output [1:0] rw_op,
  output x_op,
  output [1:0] y_op,
  output [3:0] alu_op,
  output [1:0] din_op,
  output syscall,
  output sw,
  output lw,
  output we,
  output [31:0] shamt,
  output [1:0] pc_op,
  output [4:0] rs,
  output [4:0] rt,
  output [4:0] rd,
  output [31:0] imm_15,
  output [31:0] imm_26_2
);

  wire and_1_out, and_2_out, or_4_out, signal_1_add, signal_1_addi, signal_1_addiu, signal_1_addu,
       signal_1_and, signal_1_andi, signal_1_beq, signal_1_bne, signal_1_j, signal_1_jr, signal_1_nor,
       signal_1_or, signal_1_ori, signal_1_sll, signal_1_slt, signal_1_slti, signal_1_sltu, signal_1_sra,
       signal_1_srl, signal_1_sub;
  wire [31:0] bit_extender_3_out;

  signal signal_1 (
    .PC(PC), .addi(signal_1_addi), .addiu(signal_1_addiu), .andi(signal_1_andi), .ori(signal_1_ori),
    .lw(din_op[0]), .sw(sw), .beq(signal_1_beq), .bne(signal_1_bne), .slti(signal_1_slti), .j(signal_1_j),
    .jal(din_op[1]), .add(signal_1_add), .addu(signal_1_addu), .\and (signal_1_and), .sll(signal_1_sll),
    .sra(signal_1_sra), .srl(signal_1_srl), .sub(signal_1_sub), .\or (signal_1_or), .\nor (signal_1_nor),
    .slt(signal_1_slt), .sltu(signal_1_sltu), .syscall(syscall), .jr(signal_1_jr));
  assign shamt = {{27{1'b0}}, PC[10:6]};  // Bit_Extender bit_extender_1
  assign imm_15 = {{16{PC[15]}}, PC[15:0]};  // Bit_Extender bit_extender_2
  assign bit_extender_3_out = {{6{1'b0}}, PC[25:0]};  // Bit_Extender bit_extender_3
  or or_1 (rw_op[0], signal_1_addi, signal_1_addiu, signal_1_andi, signal_1_ori, din_op[0], sw);
  Shifter #(.width(32)) shifter_1 (.in(bit_extender_3_out), .\dist (5'b00010), .out(imm_26_2));
  or or_2 (x_op, signal_1_sll, signal_1_sra, signal_1_srl);
  or or_3 (y_op[1], signal_1_addi, signal_1_addiu, signal_1_andi, signal_1_ori, din_op[0], sw, signal_1_slti);
  OP_control op_control_1 (
    .ADD(signal_1_add), .ADDU(signal_1_addu), .ADDI(signal_1_addi), .ADDIU(signal_1_addiu),
    .AND(signal_1_and), .ANDI(signal_1_andi), .LW(din_op[0]), .SW(sw), .SRL(signal_1_srl),
    .SRA(signal_1_sra), .OR(signal_1_or), .ORI(signal_1_ori), .NOR(signal_1_nor), .SLT(signal_1_slt),
    .SLTI(signal_1_slti), .SLTU(signal_1_sltu), .SUB(signal_1_sub), .out_19(alu_op), .SLL(signal_1_sll));
  and and_1 (and_1_out, signal_1_beq, equal);
  and and_2 (and_2_out, ~equal, signal_1_bne);  // AND_Gate
  or or_4 (or_4_out, and_1_out, and_2_out);
  or or_5 (pc_op[1], or_4_out, signal_1_j, din_op[1]);
  or or_6 (pc_op[0], or_4_out, signal_1_jr);
  nor nor_1 (we, syscall, signal_1_jr, sw, signal_1_bne, signal_1_beq, signal_1_j);

  assign lw = din_op[0];
  assign rd = PC[15:11];
  assign rs = PC[25:21];
  assign rt = PC[20:16];
  assign rw_op[1] = din_op[1];
  assign y_op[0] = x_op;
endmodule
