// Logisim project CPU理想流水线.circ as structural Verilog: 12 circuits, main circuit main
module main (
);

  wire alu_1_p4, and_1_out, clock_1_out, comparator_1_eq, ex_mem_1_lw_2, ex_mem_1_sw_2, id_ex_1_lw_2,
       id_ex_1_sw_2, id_ex_1_x_op_2, main_control_1_lw, main_control_1_sw, main_control_1_syscall,
       main_control_1_we, main_control_1_x_op, multiplexer_1_out;
  wire [1:0] id_ex_1_y_op_2, main_control_1_din_op, main_control_1_pc_op, main_control_1_rw_op,
       main_control_1_y_op;
  wire [3:0] id_ex_1_alu_op_2, main_control_1_alu_op;
  wire [4:0] ex_mem_1_rw_2, id_ex_1_rw, main_1_p3, main_control_1_rd, main_control_1_rs, main_control_1_rt,
       multiplexer_3_out;
  wire [31:0] adder_1_out, adder_2_out, alu_1_p5, and_2_out, counter_1_q, ex_mem_1_d_2, ex_mem_1_pc_2,
       ex_mem_1_r_2, id_ex_1_imm_15_2, id_ex_1_imm_exp_2, id_ex_1_pc_2, id_ex_1_r1_2, id_ex_1_r2_2,
       id_ex_1_shamt_2, if_id_1_d_2, if_id_1_pc_2, if_id_1_pc_31_28_2, main_1_p5, main_1_p9, main_1_p10,
       main_control_1_imm_15, main_control_1_imm_26_2, main_control_1_shamt, mem_wb_1_d_2, mem_wb_1_pc_2,
       mem_wb_1_r_2, multiplexer_2_out, multiplexer_4_out, multiplexer_5_out, or_1_out, ram_1_data, reg2,
       reg4, register_1_q, rom_1_data, shifter_1_out;

  Clock clock_1 (.out(clock_1_out));
  Multiplexer #(.enable("false")) multiplexer_1 (
    .in0(clock_1_out), .in1(1'b1), .out(multiplexer_1_out), .sel(and_1_out));
  Counter #(.width(32), .max('hffffffff)) counter_1 (
    .load(1'b0), .count(1'b1), .Q(counter_1_q), .clk(multiplexer_1_out));  // open: D, carry, clr
  Register #(.width(32), .trigger("falling")) register_1 (
    .D(multiplexer_2_out), .Q(register_1_q), .clk(multiplexer_1_out));  // open: en, clr
  // Probe on counter_1_q
  and and_1 (and_1_out, main_control_1_syscall, comparator_1_eq);
  Comparator #(.width(32)) comparator_1 (.a(32'ha), .b(reg2), .eq(comparator_1_eq));  // open: gt, lt
  Adder #(.width(32)) adder_1 (.a(32'h4), .b(register_1_q), .out(adder_1_out));  // open: cin, cout
  assign and_2_out = register_1_q & 32'hf0000000;  // AND_Gate and_2, 32 bits wide
  ROM #(.addrWidth(10), .dataWidth(32)) rom_1 (.addr(register_1_q[11:2]), .data(rom_1_data), .sel(1'b1));
  Multiplexer #(.select(2), .width(32), .enable("false")) multiplexer_2 (
    .in0(mem_wb_1_pc_2), .in1(id_ex_1_r1_2), .in2(or_1_out), .in3(id_ex_1_imm_exp_2),
    .out(multiplexer_2_out), .sel(main_control_1_pc_op));
  IF_ID if_id_1 (
    .PC(adder_1_out), .D(rom_1_data), .PC_2(if_id_1_pc_2), .D_2(if_id_1_d_2), .in_1(multiplexer_1_out),
    .PC_31_28(and_2_out), .PC_31_28_2(if_id_1_pc_31_28_2));
  main_control main_control_1 (
    .PC(if_id_1_d_2), .rw_op(main_control_1_rw_op), .x_op(main_control_1_x_op), .y_op(main_control_1_y_op),
    .alu_op(main_control_1_alu_op), .syscall(main_control_1_syscall), .sw(main_control_1_sw),
    .lw(main_control_1_lw), .rs(main_control_1_rs), .rt(main_control_1_rt), .rd(main_control_1_rd),
    .imm_15(main_control_1_imm_15), .shamt(main_control_1_shamt), .imm_26_2(main_control_1_imm_26_2),
    .equal(alu_1_p4), .pc_op(main_control_1_pc_op), .din_op(main_control_1_din_op), .we(main_control_1_we));
  Hex_Digit_Display hex_digit_display_1 (.value(reg4[27:24]));  // open: dp
  Hex_Digit_Display hex_digit_display_2 (.value(reg4[31:28]));  // open: dp
  assign or_1_out = if_id_1_pc_31_28_2 | main_control_1_imm_26_2;  // OR_Gate or_1, 32 bits wide
  Hex_Digit_Display hex_digit_display_3 (.value(reg4[23:20]));  // open: dp
  Hex_Digit_Display hex_digit_display_4 (.value(reg4[19:16]));  // open: dp
  Hex_Digit_Display hex_digit_display_5 (.value(reg4[11:8]));  // open: dp
  Hex_Digit_Display hex_digit_display_6 (.value(reg4[15:12]));  // open: dp
  Hex_Digit_Display hex_digit_display_7 (.value(reg4[7:4]));  // open: dp
  Hex_Digit_Display hex_digit_display_8 (.value(reg4[3:0]));  // open: dp
  Shifter #(.width(32)) shifter_1 (.in(main_control_1_imm_15), .\dist (5'b00010), .out(shifter_1_out));
  Multiplexer #(.select(2), .width(5), .enable("false")) multiplexer_3 (
    .in0(main_control_1_rd), .in1(main_control_1_rt), .in2({5{1'b1}}), .out(multiplexer_3_out),
    .sel(main_control_1_rw_op));  // open: in3
  Adder #(.width(32)) adder_2 (.a(if_id_1_pc_2), .b(shifter_1_out), .out(adder_2_out));  // open: cin, cout
  // regfile_main main_1: pin names not known; wires that end beside it: main_control_1_rs, main_control_1_rt, main_1_p3, reg2, main_1_p5, reg4, main_control_1_we, multiplexer_1_out, main_1_p9, main_1_p10
  ID_EX id_ex_1 (
    .imm_exp(adder_2_out), .imm_15(main_control_1_imm_15), .x_op(main_control_1_x_op), .R1(main_1_p9),
    .R2(main_1_p10), .shamt(main_control_1_shamt), .y_op(main_control_1_y_op),
    .alu_op(main_control_1_alu_op), .lw(main_control_1_lw), .sw(main_control_1_sw),
    .imm_exp_2(id_ex_1_imm_exp_2), .imm_15_2(id_ex_1_imm_15_2), .x_op_2(id_ex_1_x_op_2), .R1_2(id_ex_1_r1_2),
    .R2_2(id_ex_1_r2_2), .shamt_2(id_ex_1_shamt_2), .y_op_2(id_ex_1_y_op_2), .alu_op_2(id_ex_1_alu_op_2),
    .lw_2(id_ex_1_lw_2), .sw_2(id_ex_1_sw_2), .in_1(multiplexer_1_out), .pc(if_id_1_pc_2),
    .pc_2(id_ex_1_pc_2), .r_prime_w(multiplexer_3_out), .rw(id_ex_1_rw));
  Multiplexer #(.width(32), .enable("false")) multiplexer_4 (
    .in0(id_ex_1_r1_2), .in1(id_ex_1_r2_2), .out(multiplexer_4_out), .sel(id_ex_1_x_op_2));
  Multiplexer #(.select(2), .width(32), .enable("false")) multiplexer_5 (
    .in0(id_ex_1_r2_2), .in1(id_ex_1_shamt_2), .in2(id_ex_1_imm_15_2), .out(multiplexer_5_out),
    .sel(id_ex_1_y_op_2));  // open: in3
  // ALU alu_1: pin names not known; wires that end beside it: multiplexer_4_out, multiplexer_5_out, id_ex_1_alu_op_2, alu_1_p4, alu_1_p5
  EX_MEM ex_mem_1 (
    .pc(id_ex_1_pc_2), .R(alu_1_p5), .D(id_ex_1_r2_2), .lw(id_ex_1_lw_2), .sw(id_ex_1_sw_2),
    .pc_2(ex_mem_1_pc_2), .R_2(ex_mem_1_r_2), .D_2(ex_mem_1_d_2), .lw_2(ex_mem_1_lw_2), .sw_2(ex_mem_1_sw_2),
    .in_1(multiplexer_1_out), .rw(id_ex_1_rw), .rw_2(ex_mem_1_rw_2));
  RAM #(.addrWidth(10), .dataWidth(32), .bus("separate")) ram_1 (
    .addr(ex_mem_1_r_2[11:2]), .din(ex_mem_1_d_2), .data(ram_1_data), .str(ex_mem_1_sw_2), .sel(1'b1),
    .clk(multiplexer_1_out), .ld(ex_mem_1_lw_2));  // open: clr
  MEM_WB mem_wb_1 (
    .R(ex_mem_1_r_2), .D(ram_1_data), .PC(ex_mem_1_pc_2), .R_2(mem_wb_1_r_2), .D_2(mem_wb_1_d_2),
    .PC_2(mem_wb_1_pc_2), .in_1(multiplexer_1_out), .r_prime_w(ex_mem_1_rw_2), .rw(main_1_p3));
  Multiplexer #(.select(2), .width(32), .enable("false")) multiplexer_6 (
    .in0(mem_wb_1_r_2), .in1(mem_wb_1_d_2), .in2(mem_wb_1_pc_2), .out(main_1_p5), .sel(main_control_1_din_op));  // open: in3

  // Notes on the sheet:
  //   contents of rom_1 (hex, n*v repeats v):
  //   20100000 20110000 20120000 20130000 36100000 36310001 36520002 36730003 ae100000 ae110004 ae120008
  //   ae13000c 2002000a 20110000 20120000 20130000 c
endmodule

module \I型指令  (
  input  op0,
  input  op1,
  input  op2,
  input  op3,
  input  op4,
  input  op5,
  output addi,
  output addiu,
  output andi,
  output ori,
  output lw,
  output sw,
  output beq,
  output bne,
  output slti
);

  wire not_1_out, not_2_out, not_3_out, not_4_out, not_5_out, not_6_out, not_7_out, not_8_out, not_9_out,
       not_10_out, not_11_out, not_12_out, not_13_out, not_14_out, not_15_out, not_16_out, not_17_out,
       not_18_out, not_19_out, not_20_out, not_21_out, not_22_out, not_23_out, not_24_out, not_25_out,
       not_26_out, not_27_out, not_28_out, not_29_out, not_30_out, not_31_out, not_32_out, not_33_out,
       not_34_out;

  not not_1 (not_1_out, op0);
  not not_2 (not_2_out, op1);
  not not_3 (not_3_out, op3);
  not not_4 (not_4_out, op4);
  not not_5 (not_5_out, op5);
  not not_6 (not_6_out, op0);
  not not_7 (not_7_out, op1);
  not not_8 (not_8_out, op3);
  not not_9 (not_9_out, op4);
  not not_10 (not_10_out, op0);
  not not_11 (not_11_out, op1);
  not not_12 (not_12_out, op4);
  not not_13 (not_13_out, op5);
  not not_14 (not_14_out, op0);
  not not_15 (not_15_out, op1);
  not not_16 (not_16_out, op4);
  not not_17 (not_17_out, op1);
  not not_18 (not_18_out, op2);
  not not_19 (not_19_out, op3);
  not not_20 (not_20_out, op1);
  not not_21 (not_21_out, op3);
  not not_22 (not_22_out, op0);
  not not_23 (not_23_out, op1);
  not not_24 (not_24_out, op2);
  not not_25 (not_25_out, op4);
  not not_26 (not_26_out, op5);
  not not_27 (not_27_out, op0);
  not not_28 (not_28_out, op1);
  not not_29 (not_29_out, op2);
  not not_30 (not_30_out, op4);
  not not_31 (not_31_out, op0);
  not not_32 (not_32_out, op1);
  not not_33 (not_33_out, op3);
  not not_34 (not_34_out, op5);
  and and_1 (addi, not_1_out, not_2_out, op2, not_3_out, not_4_out, not_5_out);
  and and_2 (addiu, not_6_out, not_7_out, op2, not_8_out, not_9_out, op5);
  and and_3 (andi, not_10_out, not_11_out, op2, op3, not_12_out, not_13_out);
  and and_4 (ori, not_14_out, not_15_out, op2, op3, not_16_out, op5);
  and and_5 (lw, op0, not_17_out, not_18_out, not_19_out, op4, op5);
  and and_6 (sw, op0, not_20_out, op2, not_21_out, op4, op5);
  and and_7 (beq, not_22_out, not_23_out, not_24_out, op3, not_25_out, not_26_out);
  and and_8 (bne, not_27_out, not_28_out, not_29_out, op3, not_30_out, op5);
  and and_9 (slti, not_31_out, not_32_out, op2, not_33_out, op4, not_34_out);
endmodule

module \R型指令  (
  input  funct0,
  input  funct1,
  input  funct2,
  input  funct3,
  input  funct4,
  input  funct5,
  input  in_7,
  output add,
  output addu,
  output \and ,
  output sll,
  output sra,
  output srl,
  output sub,
  output \or ,
  output \nor ,
  output slt,
  output sltu,
  output syscall,
  output jr
);

  wire and_1_out, and_2_out, and_3_out, and_4_out, and_5_out, and_6_out, and_7_out, and_8_out, and_9_out,
       and_10_out, and_11_out, and_12_out, and_13_out, not_1_out, not_2_out, not_3_out, not_4_out, not_5_out,
       not_6_out, not_7_out, not_8_out, not_9_out, not_10_out, not_11_out, not_12_out, not_13_out,
       not_14_out, not_15_out, not_16_out, not_17_out, not_18_out, not_19_out, not_20_out, not_21_out,
       not_22_out, not_23_out, not_24_out, not_25_out, not_26_out, not_27_out, not_28_out, not_29_out,
       not_30_out, not_31_out, not_32_out, not_33_out, not_34_out, not_35_out, not_36_out, not_37_out,
       not_38_out, not_39_out, not_40_out, not_41_out, not_42_out, not_43_out, not_44_out, not_45_out,
       not_46_out, not_47_out, not_48_out, not_49_out, not_50_out, not_51_out;

  not not_1 (not_1_out, funct1);
  not not_2 (not_2_out, funct2);
  not not_3 (not_3_out, funct3);
  not not_4 (not_4_out, funct4);
  not not_5 (not_5_out, funct5);
  not not_6 (not_6_out, funct1);
  not not_7 (not_7_out, funct2);
  not not_8 (not_8_out, funct3);
  not not_9 (not_9_out, funct4);
  not not_10 (not_10_out, funct1);
  not not_11 (not_11_out, funct2);
  not not_12 (not_12_out, funct4);
  not not_13 (not_13_out, funct5);
  not not_14 (not_14_out, funct0);
  not not_15 (not_15_out, funct1);
  not not_16 (not_16_out, funct2);
  not not_17 (not_17_out, funct3);
  not not_18 (not_18_out, funct4);
  not not_19 (not_19_out, funct5);
  not not_20 (not_20_out, funct0);
  not not_21 (not_21_out, funct1);
  not not_22 (not_22_out, funct2);
  not not_23 (not_23_out, funct3);
  not not_24 (not_24_out, funct0);
  not not_25 (not_25_out, funct1);
  not not_26 (not_26_out, funct2);
  not not_27 (not_27_out, funct3);
  not not_28 (not_28_out, funct5);
  not not_29 (not_29_out, funct1);
  not not_30 (not_30_out, funct2);
  not not_31 (not_31_out, funct3);
  not not_32 (not_32_out, funct5);
  not not_33 (not_33_out, funct1);
  not not_34 (not_34_out, funct2);
  not not_35 (not_35_out, funct4);
  not not_36 (not_36_out, funct1);
  not not_37 (not_37_out, funct2);
  not not_38 (not_38_out, funct1);
  not not_39 (not_39_out, funct3);
  not not_40 (not_40_out, funct5);
  not not_41 (not_41_out, funct1);
  not not_42 (not_42_out, funct3);
  not not_43 (not_43_out, funct0);
  not not_44 (not_44_out, funct1);
  not not_45 (not_45_out, funct4);
  not not_46 (not_46_out, funct5);
  not not_47 (not_47_out, funct0);
  not not_48 (not_48_out, funct1);
  not not_49 (not_49_out, funct3);
  not not_50 (not_50_out, funct4);
  not not_51 (not_51_out, funct5);
  and and_1 (and_1_out, funct0, not_1_out, not_2_out, not_3_out, not_4_out, not_5_out);
  and and_2 (and_2_out, funct0, not_6_out, not_7_out, not_8_out, not_9_out, funct5);
  and and_3 (and_3_out, funct0, not_10_out, not_11_out, funct3, not_12_out, not_13_out);
  and and_4 (and_4_out, not_14_out, not_15_out, not_16_out, not_17_out, not_18_out, not_19_out);
  and and_5 (and_5_out, not_20_out, not_21_out, not_22_out, not_23_out, funct4, funct5);
  and and_6 (and_6_out, not_24_out, not_25_out, not_26_out, not_27_out, funct4, not_28_out);
  and and_7 (and_7_out, funct0, not_29_out, not_30_out, not_31_out, funct4, not_32_out);
  and and_8 (and_8_out, funct0, not_33_out, not_34_out, funct3, not_35_out, funct5);
  and and_9 (and_9_out, funct0, not_36_out, not_37_out, funct3, funct4, funct5);
  and and_10 (and_10_out, funct0, not_38_out, funct2, not_39_out, funct4, not_40_out);
  and and_11 (and_11_out, funct0, not_41_out, funct2, not_42_out, funct4, funct5);
  and and_12 (and_12_out, not_43_out, not_44_out, funct2, funct3, not_45_out, not_46_out);
  and and_13 (and_13_out, not_47_out, not_48_out, funct2, not_49_out, not_50_out, not_51_out);
  and and_14 (add, and_1_out, in_7);
  and and_15 (addu, and_2_out, in_7);
  and and_16 (\and , and_3_out, in_7);
  and and_17 (sll, and_4_out, in_7);
  and and_18 (sra, and_5_out, in_7);
  and and_19 (srl, and_6_out, in_7);
  and and_20 (sub, and_7_out, in_7);
  and and_21 (\or , and_8_out, in_7);
  and and_22 (\nor , and_9_out, in_7);
  and and_23 (slt, and_10_out, in_7);
  and and_24 (sltu, and_11_out, in_7);
  and and_25 (syscall, and_12_out, in_7);
  and and_26 (jr, and_13_out, in_7);
endmodule

module \j型指令  (
  input  op0,
  input  op1,
  input  op2,
  input  op3,
  input  op4,
  input  op5,
  output j,
  output jal
);

  wire not_1_out, not_2_out, not_3_out, not_4_out, not_5_out, not_6_out, not_7_out, not_8_out, not_9_out;

  not not_1 (not_1_out, op0);
  not not_2 (not_2_out, op1);
  not not_3 (not_3_out, op2);
  not not_4 (not_4_out, op3);
  not not_5 (not_5_out, op5);
  not not_6 (not_6_out, op0);
  not not_7 (not_7_out, op1);
  not not_8 (not_8_out, op2);
  not not_9 (not_9_out, op3);
  and and_1 (j, not_1_out, not_2_out, not_3_out, not_4_out, op4, not_5_out);
  and and_2 (jal, not_6_out, not_7_out, not_8_out, not_9_out, op4, op5);
endmodule

module signal (
  input  [31:0] PC,
  output add,
  output addu,
  output \and ,
  output sll,
  output sra,
  output srl,
  output sub,
  output \or ,
  output \nor ,
  output slt,
  output sltu,
  output syscall,
  output jr,
  output j,
  output jal,
  output addi,
  output addiu,
  output andi,
  output ori,
  output lw,
  output sw,
  output beq,
  output bne,
  output slti
);

  wire and_1_out;

  and and_1 (and_1_out, ~PC[31], ~PC[30], ~PC[29], ~PC[28], ~PC[27], ~PC[26]);  // AND_Gate
  \R型指令  \r型指令_1  (
    .funct0(PC[5]), .funct1(PC[4]), .funct2(PC[3]), .funct3(PC[2]), .funct4(PC[1]), .funct5(PC[0]),
    .in_7(and_1_out), .add(add), .addu(addu), .\and (\and ), .sll(sll), .sra(sra), .srl(srl), .sub(sub),
    .\or (\or ), .\nor (\nor ), .slt(slt), .sltu(sltu), .syscall(syscall), .jr(jr));
  \j型指令  \j型指令_1  (
    .op0(PC[31]), .op1(PC[30]), .op2(PC[29]), .op3(PC[28]), .op4(PC[27]), .op5(PC[26]), .j(j), .jal(jal));
  \I型指令  \i型指令_1  (
    .op0(PC[31]), .op1(PC[30]), .op2(PC[29]), .op3(PC[28]), .op4(PC[27]), .op5(PC[26]), .addi(addi),
    .addiu(addiu), .andi(andi), .ori(ori), .lw(lw), .sw(sw), .beq(beq), .bne(bne), .slti(slti));
endmodule

module OP_control (
  input  SLL,
  input  ADD,
  input  ADDU,
  input  ADDI,
  input  ADDIU,
  input  AND,
  input  ANDI,
  input  LW,
  input  SW,
  input  SRL,
  input  SRA,
  input  OR,
  input  ORI,
  input  NOR,
  input  SLT,
  input  SLTI,
  input  SLTU,
  input  SUB,
  output [3:0] out_19
);

  and and_1 (out_19[0], ~SUB, ~SLL, ~SRL, ~OR, ~ORI);  // AND_Gate
  and and_2 (out_19[1], ~SLL, ~SRA, ~ADD, ~ADDI, ~ADDU, ~ORI, ~ADDIU, ~SW, ~LW, ~OR, ~NOR);  // AND_Gate
  and and_3 (out_19[2], ~SLL, ~NOR, ~SRA, ~SLTU, ~SRL, ~SLTI, ~ORI, ~SLT, ~OR);  // AND_Gate
  and and_4 (out_19[3], ~SLL, ~SRA, ~SRL, ~ADD, ~ADDI, ~ADDU, ~ADDIU, ~SW, ~LW, ~SUB, ~AND, ~ANDI);  // AND_Gate
endmodule

module main_control (
  input  equal,
  input  [31:0] PC,
  output [1:0] rw_op,
  output x_op,
  output [1:0] y_op,
  output [3:0] alu_op,
  output [1:0] din_op,
  output syscall,
  output sw,
  output lw,
  output we,
  output [31:0] shamt,
  output [1:0] pc_op,
  output [4:0] rs,
  output [4:0] rt,
  output [4:0] rd,
  output [31:0] imm_15,
  output [31:0] imm_26_2
);

  wire and_1_out, and_2_out, or_4_out, signal_1_add, signal_1_addi, signal_1_addiu, signal_1_addu,
       signal_1_and, signal_1_andi, signal_1_beq, signal_1_bne, signal_1_j, signal_1_jr, signal_1_nor,
       signal_1_or, signal_1_ori, signal_1_sll, signal_1_slt, signal_1_slti, signal_1_sltu, signal_1_sra,
       signal_1_srl, signal_1_sub;
  wire [31:0] bit_extender_3_out;

  signal signal_1 (
    .PC(PC), .addi(signal_1_addi), .addiu(signal_1_addiu), .andi(signal_1_andi), .ori(signal_1_ori),
    .lw(din_op[0]), .sw(sw), .beq(signal_1_beq), .bne(signal_1_bne), .slti(signal_1_slti), .j(signal_1_j),
    .jal(din_op[1]), .add(signal_1_add), .addu(signal_1_addu), .\and (signal_1_and), .sll(signal_1_sll),
    .sra(signal_1_sra), .srl(signal_1_srl), .sub(signal_1_sub), .\or (signal_1_or), .\nor (signal_1_nor),
    .slt(signal_1_slt), .sltu(signal_1_sltu), .syscall(syscall), .jr(signal_1_jr));
  assign shamt = {{27{1'b0}}, PC[10:6]};  // Bit_Extender bit_extender_1
  assign imm_15 = {{16{PC[15]}}, PC[15:0]};  // Bit_Extender bit_extender_2
  assign bit_extender_3_out = {{6{1'b0}}, PC[25:0]};  // Bit_Extender bit_extender_3
  or or_1 (rw_op[0], signal_1_addi, signal_1_addiu, signal_1_andi, signal_1_ori, din_op[0], sw);
  Shifter #(.width(32)) shifter_1 (.in(bit_extender_3_out), .\dist (5'b00010), .out(imm_26_2));
  or or_2 (x_op, signal_1_sll, signal_1_sra, signal_1_srl);
  or or_3 (y_op[1], signal_1_addi, signal_1_addiu, signal_1_andi, signal_1_ori, din_op[0], sw, signal_1_slti);
  OP_control op_control_1 (
    .ADD(signal_1_add), .ADDU(signal_1_addu), .ADDI(signal_1_addi), .ADDIU(signal_1_addiu),
    .AND(signal_1_and), .ANDI(signal_1_andi), .LW(din_op[0]), .SW(sw), .SRL(signal_1_srl),
    .SRA(signal_1_sra), .OR(signal_1_or), .ORI(signal_1_ori), .NOR(signal_1_nor), .SLT(signal_1_slt),
    .SLTI(signal_1_slti), .SLTU(signal_1_sltu), .SUB(signal_1_sub), .out_19(alu_op), .SLL(signal_1_sll));
  and and_1 (and_1_out, signal_1_beq, equal);
  and and_2 (and_2_out, ~equal, signal_1_bne);  // AND_Gate
  or or_4 (or_4_out, and_1_out, and_2_out);
  or or_5 (pc_op[1], or_4_out, signal_1_j, din_op[1]);
  or or_6 (pc_op[0], or_4_out, signal_1_jr);
  nor nor_1 (we, syscall, signal_1_jr, sw, signal_1_bne, signal_1_beq, signal_1_j);

  assign lw = din_op[0];
  assign rd = PC[15:11];
  assign rs = PC[25:21];
  assign rt = PC[20:16];
  assign rw_op[1] = din_op[1];
  assign y_op[0] = x_op;
endmodule

module IF_ID (
  input  in_1,
  input  [31:0] PC,
  input  [31:0] PC_31_28,
  input  [31:0] D,
  output [31:0] PC_2,
  output [31:0] PC_31_28_2,
  output [31:0] D_2
);

  Register #(.width(32)) register_1 (.D(PC), .Q(PC_2), .clk(in_1));  // open: en, clr
  Register #(.width(32)) register_2 (.D(PC_31_28), .Q(PC_31_28_2), .clk(in_1));  // open: en, clr
  Register #(.width(32)) register_3 (.D(D), .Q(D_2), .clk(in_1));  // open: en, clr
endmodule

module ID_EX (
  input  in_1,
  input  [31:0] pc,
  input  [31:0] imm_exp,
  input  [31:0] imm_15,
  input  x_op,
  input  [31:0] R1,
  input  [31:0] R2,
  input  [31:0] shamt,
  input  [1:0] y_op,
  input  [3:0] alu_op,
  input  [4:0] r_prime_w,
  input  lw,
  input  sw,
  output [31:0] pc_2,
  output [31:0] imm_exp_2,
  output [31:0] imm_15_2,
  output x_op_2,
  output [31:0] R1_2,
  output [31:0] R2_2,
  output [31:0] shamt_2,
  output [1:0] y_op_2,
  output [3:0] alu_op_2,
  output [4:0] rw,
  output lw_2,
  output sw_2
);

  Register #(.width(32)) register_1 (.D(pc), .Q(pc_2), .clk(in_1));  // open: en, clr
  Register #(.width(32)) register_2 (.D(imm_exp), .Q(imm_exp_2), .clk(in_1));  // open: en, clr
  Register #(.width(32)) register_3 (.D(imm_15), .Q(imm_15_2), .clk(in_1));  // open: en, clr
  Register #(.width(1)) register_4 (.D(x_op), .Q(x_op_2), .clk(in_1));  // open: en, clr
  Register #(.width(32)) register_5 (.D(R1), .Q(R1_2), .clk(in_1));  // open: en, clr
  Register #(.width(32)) register_6 (.D(R2), .Q(R2_2), .clk(in_1));  // open: en, clr
  Register #(.width(32)) register_7 (.D(shamt), .Q(shamt_2), .clk(in_1));  // open: en, clr
  Register #(.width(2)) register_8 (.D(y_op), .Q(y_op_2), .clk(in_1));  // open: en, clr
  Register #(.width(4)) register_9 (.D(alu_op), .Q(alu_op_2), .clk(in_1));  // open: en, clr
  Register #(.width(5)) register_10 (.D(r_prime_w), .Q(rw), .clk(in_1));  // open: en, clr
  Register #(.width(1)) register_11 (.D(lw), .Q(lw_2), .clk(in_1));  // open: en, clr
  Register #(.width(1)) register_12 (.D(sw), .Q(sw_2), .clk(in_1));  // open: en, clr
endmodule

module EX_MEM (
  input  in_1,
  input  [31:0] pc,
  input  [31:0] R,
  input  [31:0] D,
  input  [4:0] rw,
  input  lw,
  input  sw,
  output [31:0] pc_2,
  output [31:0] R_2,
  output [31:0] D_2,
  output [4:0] rw_2,
  output lw_2,
  output sw_2
);

  Register #(.width(32)) register_1 (.D(pc), .Q(pc_2), .clk(in_1));  // open: en, clr
  Register #(.width(32)) register_2 (.D(R), .Q(R_2), .clk(in_1));  // open: en, clr
  Register #(.width(32)) register_3 (.D(D), .Q(D_2), .clk(in_1));  // open: en, clr
  Register #(.width(5)) register_4 (.D(rw), .Q(rw_2), .clk(in_1));  // open: en, clr
  Register #(.width(1)) register_5 (.D(lw), .Q(lw_2), .clk(in_1));  // open: en, clr
  Register #(.width(1)) register_6 (.D(sw), .Q(sw_2), .clk(in_1));  // open: en, clr
endmodule

module MEM_WB (
  input  in_1,
  input  [31:0] R,
  input  [31:0] D,
  input  [31:0] PC,
  input  [4:0] r_prime_w,
  output [31:0] R_2,
  output [31:0] D_2,
  output [31:0] PC_2,
  output [4:0] rw
);

  Register #(.width(32)) register_1 (.D(R), .Q(R_2), .clk(in_1));  // open: en, clr
  Register #(.width(32)) register_2 (.D(D), .Q(D_2), .clk(in_1));  // open: en, clr
  Register #(.width(32)) register_3 (.D(PC), .Q(PC_2), .clk(in_1));  // open: en, clr
  Register #(.width(5)) register_4 (.D(r_prime_w), .Q(rw), .clk(in_1));  // open: en, clr
endmodule

module conflict (
  input  [4:0] rw1,
  input  [4:0] rs,
  input  [4:0] rt,
  input  [4:0] rw2,
  input  [31:0] PC,
  output conf,
  output j
);

  wire and_1_out, and_2_out, comparator_1_eq, comparator_2_eq, comparator_3_eq, comparator_4_eq,
       comparator_5_eq, comparator_6_eq, multiplexer_1_out, multiplexer_2_out, multiplexer_3_out, not_1_out,
       not_2_out, or_1_out, or_2_out, or_7_out, rs_op, rs_op_or_rt_op, rt_op, signal_1_add, signal_1_addi,
       signal_1_addiu, signal_1_addu, signal_1_and, signal_1_andi, signal_1_beq, signal_1_bne, signal_1_j,
       signal_1_jal, signal_1_jr, signal_1_lw, signal_1_nor, signal_1_or, signal_1_ori, signal_1_sll,
       signal_1_slt, signal_1_slti, signal_1_sltu, signal_1_sra, signal_1_srl, signal_1_sub, signal_1_sw;

  signal signal_1 (
    .PC(PC), .addi(signal_1_addi), .addiu(signal_1_addiu), .andi(signal_1_andi), .ori(signal_1_ori),
    .lw(signal_1_lw), .sw(signal_1_sw), .beq(signal_1_beq), .bne(signal_1_bne), .slti(signal_1_slti),
    .j(signal_1_j), .jal(signal_1_jal), .add(signal_1_add), .addu(signal_1_addu), .\and (signal_1_and),
    .sll(signal_1_sll), .sra(signal_1_sra), .srl(signal_1_srl), .sub(signal_1_sub), .\or (signal_1_or),
    .\nor (signal_1_nor), .slt(signal_1_slt), .sltu(signal_1_sltu), .jr(signal_1_jr));  // open: syscall
  not not_1 (not_1_out, comparator_1_eq);
  Comparator #(.width(5)) comparator_1 (.a(rs), .b({5{1'b0}}), .eq(comparator_1_eq));  // open: gt, lt
  not not_2 (not_2_out, comparator_2_eq);
  Comparator #(.width(5)) comparator_2 (.a(rt), .b({5{1'b0}}), .eq(comparator_2_eq));  // open: gt, lt
  Comparator #(.width(5)) comparator_3 (.a(rs), .b(rw1), .eq(comparator_3_eq));  // open: gt, lt
  Comparator #(.width(5)) comparator_4 (.a(rt), .b(rw1), .eq(comparator_4_eq));  // open: gt, lt
  Comparator #(.width(5)) comparator_5 (.a(rs), .b(rw2), .eq(comparator_5_eq));  // open: gt, lt
  Comparator #(.width(5)) comparator_6 (.a(rt), .b(rw2), .eq(comparator_6_eq));  // open: gt, lt
  and and_1 (and_1_out, not_1_out, or_1_out);
  or or_1 (or_1_out, comparator_3_eq, comparator_5_eq);
  and and_2 (and_2_out, not_2_out, or_2_out);
  or or_2 (or_2_out, comparator_4_eq, comparator_6_eq);
  or or_3 (rt_op, signal_1_sll, signal_1_sra, signal_1_srl);
  or or_4 (rs_op_or_rt_op, signal_1_sw, signal_1_beq, signal_1_bne, signal_1_add, signal_1_addu, signal_1_and, signal_1_sub, signal_1_or, signal_1_nor, signal_1_slt, signal_1_sltu);
  or or_5 (rs_op, signal_1_addi, signal_1_addiu, signal_1_andi, signal_1_ori, signal_1_lw, signal_1_slti, signal_1_jr);
  or or_6 (j, signal_1_j, signal_1_jal);
  or or_7 (or_7_out, and_1_out, and_2_out);
  Multiplexer #(.enable("false")) multiplexer_1 (.in0(1'b0), .in1(and_1_out), .out(multiplexer_1_out), .sel(rs_op));
  Multiplexer #(.enable("false")) multiplexer_2 (
    .in0(1'b0), .in1(or_7_out), .out(multiplexer_2_out), .sel(rs_op_or_rt_op));
  Multiplexer #(.enable("false")) multiplexer_3 (.in0(1'b0), .in1(and_2_out), .out(multiplexer_3_out), .sel(rt_op));
  or or_8 (conf, multiplexer_1_out, multiplexer_2_out, multiplexer_3_out);
endmodule
